# Fritzing sketch Komoot_BLE (saved by Fritzing 0.9.3b)
breadboards: 1

parts:
  U1 = lolin
  Squix1 = OLED 0.96" 128x64 I2C SSD1306
  R1 = Resistor [tolerance=±1% resistance=330k package=THT]
  R2 = Resistor [tolerance=±1% resistance=110k package=THT]

nets (from the schematic view):
  N1: U1.connector7, R1.Pin_0, R2.Pin_0
  N2: U1.connector15, R2.Pin_1
  N3: U1.connector16, R1.Pin_1
  N4: U1.connector30, Squix1.GND
  N5: U1.connector32, Squix1.SCA
  N6: U1.connector33, Squix1.SCL
  N7: U1.connector34, Squix1.VCC

notes:
  Touch-ON
